# Fritzing sketch daft_punk_electronic (saved by Fritzing 0.9.3b)

parts:
  Composant1 = Arduino Nano (Rev3.0)
  Composant2 = Bluetooth HC-05 Macho
  U1 = SWITCH-SPST-2 [package=switch-spst-vertical]
  VCC1 = Battery

nets:
  GND: Composant1.GND, Composant2.GND
  N1: Composant1.D2, Composant2.TXD
  N2: Composant1.D3, Composant2.RXD
  N3: Composant1.VIN, U1.P
  5V: Composant1.5V, Composant2.VCC
  N4: U1.O, VCC1.+
